// Logisim project Decodificatore3bit.circ as structural Verilog: 1 circuit, main circuit Dec3bit
module Dec3bit (
  input  in_1,
  input  [2:0] in_2,
  output out_3,
  output out_4,
  output out_5,
  output out_6,
  output out_7,
  output out_8,
  output out_9,
  output out_10
);

  wire and_1_out, and_2_out, and_3_out, and_4_out, and_5_out, and_6_out, and_7_out, and_8_out;

  and and_1 (and_1_out, ~in_2[2], ~in_2[1], ~in_2[0]);  // AND_Gate
  and and_2 (and_2_out, ~in_2[2], ~in_2[1], in_2[0]);  // AND_Gate
  and and_3 (and_3_out, ~in_2[2], in_2[1], ~in_2[0]);  // AND_Gate
  and and_4 (and_4_out, ~in_2[2], in_2[1], in_2[0]);  // AND_Gate
  and and_5 (and_5_out, in_2[2], ~in_2[1], ~in_2[0]);  // AND_Gate
  and and_6 (and_6_out, in_2[2], ~in_2[1], in_2[0]);  // AND_Gate
  and and_7 (and_7_out, in_2[2], in_2[1], ~in_2[0]);  // AND_Gate
  and and_8 (and_8_out, in_2[2], in_2[1], in_2[0]);
  and and_9 (out_3, in_1, and_1_out);
  and and_10 (out_4, in_1, and_2_out);
  and and_11 (out_5, in_1, and_3_out);
  and and_12 (out_6, in_1, and_4_out);
  and and_13 (out_7, in_1, and_5_out);
  and and_14 (out_8, in_1, and_6_out);
  and and_15 (out_9, in_1, and_7_out);
  and and_16 (out_10, in_1, and_8_out);
endmodule
