// Logisim project Latch Set-Clear.circ as structural Verilog: 1 circuit, main circuit LATCHSet-Clear
module LATCHSet_Clear (
  input  C,
  input  S,
  output Q,
  output nQ
);

  nor nor_1 (Q, C, nQ);
  nor nor_2 (nQ, Q, S);
endmodule
