// Logisim project Notarangelo_Elisa_920295_Arch1Lab_Progetto.circ as structural Verilog: 4 circuits, main circuit main
module main (
  output out_1
);

  wire down, lose_1_out_4, or_1_out, reset, up;
  wire [4:0] _0, _1, _2, _3, _4;

  DotMatrix #(.matrixrows(5)) dotmatrix_1 (.col0(_4), .col1(_3), .col2(_2), .col3(_1), .col4(_0));
  or or_1 (or_1_out, reset, out_1);
  Button button_1 (.out(up));
  Traffic_street traffic_street_1 (.reset(or_1_out), .out_2(_4), .out_3(_3), .out_4(_2), .out_5(_1), .out_6(_0));
  Button button_2 (.out(down));
  Button button_3 (.out(reset));
  Up___Down up_down_1 (.up(down), .down(up), .reset(reset), .out_4(_2));
  Lose lose_1 (.in_1(_2), .in_2(_2), .in_3(reset), .out_4(lose_1_out_4));
  Lose lose_2 (.in_1(_2), .in_2(_2), .in_3(reset), .out_4(out_1));
  _7_Segment_Display u_7_segment_display_1 (
    .f(lose_1_out_4), .e(lose_1_out_4), .d(lose_1_out_4));  // open: g, a, b, c, dp
  _7_Segment_Display u_7_segment_display_2 (
    .f(lose_1_out_4), .a(lose_1_out_4), .b(lose_1_out_4), .e(lose_1_out_4), .d(lose_1_out_4), .c(lose_1_out_4));  // open: g, dp
  _7_Segment_Display u_7_segment_display_3 (
    .g(lose_1_out_4), .f(lose_1_out_4), .a(lose_1_out_4), .d(lose_1_out_4), .c(lose_1_out_4));  // open: b, e, dp
  _7_Segment_Display u_7_segment_display_4 (
    .g(lose_1_out_4), .f(lose_1_out_4), .a(lose_1_out_4), .e(lose_1_out_4), .d(lose_1_out_4));  // open: b, c, dp

  // Other names for the same wires on the sheet: c[4:0] = _2

  // Notes on the sheet:
  //   Display 
  //   Comandi
  //   Lose
endmodule

// traffic steet
module Traffic_street (
  input  reset,
  output [4:0] out_2,
  output [4:0] out_3,
  output [4:0] out_4,
  output [4:0] out_5,
  output [4:0] out_6
);

  wire clock_1_out, dec3bit_1_out_3, dec3bit_1_out_4, dec3bit_1_out_5, dec3bit_1_out_6, dec3bit_1_out_7;
  wire [2:0] counter_1_q;

  Clock clock_1 (.out(clock_1_out));
  Counter #(.width(3), .max('h4), .trigger("falling")) counter_1 (
    .Q(counter_1_q), .clk(clock_1_out), .clr(reset));  // open: load, D, count, carry
  Dec3bit dec3bit_1 (
    .in_1(1'b1), .in_2(counter_1_q), .out_3(dec3bit_1_out_3), .out_4(dec3bit_1_out_4),
    .out_5(dec3bit_1_out_5), .out_6(dec3bit_1_out_6), .out_7(dec3bit_1_out_7));  // open: out_8, out_9, out_10
  Multiplexer #(.width(5), .disabled(0)) multiplexer_1 (
    .in0({5{1'b0}}), .in1(5'b00100), .out(out_2), .sel(dec3bit_1_out_7));  // open: en
  Multiplexer #(.width(5), .disabled(0)) multiplexer_2 (
    .in0({5{1'b0}}), .in1(5'b00100), .out(out_3), .sel(dec3bit_1_out_6));  // open: en
  Multiplexer #(.width(5), .disabled(0)) multiplexer_3 (
    .in0({5{1'b0}}), .in1(5'b00100), .out(out_4), .sel(dec3bit_1_out_5));  // open: en
  Multiplexer #(.width(5), .disabled(0)) multiplexer_4 (
    .in0({5{1'b0}}), .in1(5'b00100), .out(out_5), .sel(dec3bit_1_out_4));  // open: en
  Multiplexer #(.width(5), .disabled(0)) multiplexer_5 (
    .in0({5{1'b0}}), .in1(5'b00100), .out(out_6), .sel(dec3bit_1_out_3));  // open: en
endmodule

// Up & DOwn
module Up___Down (
  input  up,
  input  down,
  input  reset,
  output [4:0] out_4
);

  wire and_1_out, and_2_out, and_3_out, and_4_out, and_5_out, and_6_out, and_7_out, and_8_out, and_9_out,
       and_10_out, dec3bit_1_out_3, dec3bit_1_out_4, dec3bit_1_out_5, dec3bit_1_out_6, dec3bit_1_out_7,
       or_1_out, or_2_out, or_3_out, or_4_out, or_5_out, or_6_out, or_7_out, or_8_out, or_9_out;
  wire [2:0] counter_1_q;

  or or_1 (or_1_out, up, down);
  Dec3bit dec3bit_1 (
    .in_1(1'b1), .in_2(counter_1_q), .out_3(dec3bit_1_out_3), .out_4(dec3bit_1_out_4),
    .out_5(dec3bit_1_out_5), .out_6(dec3bit_1_out_6), .out_7(dec3bit_1_out_7));  // open: out_8, out_9, out_10
  or or_2 (or_2_out, up, reset);
  Counter #(.width(3), .max('h4)) counter_1 (
    .load(or_2_out), .D(3'b000), .count(or_1_out), .Q(counter_1_q), .clk(or_3_out));  // open: carry, clr
  or or_3 (or_3_out, or_1_out, reset);
  or or_4 (or_4_out, dec3bit_1_out_3, reset);
  LATCHSet_Clear latchset_clear_1 (.C(or_5_out), .S(dec3bit_1_out_7), .Q(out_4[4]));  // open: nQ
  or or_5 (or_5_out, and_6_out, reset, and_1_out);
  or or_6 (or_6_out, and_7_out, reset, and_2_out);
  or or_7 (or_7_out, and_8_out, reset, and_3_out);
  or or_8 (or_8_out, and_9_out, reset, and_4_out);
  or or_9 (or_9_out, and_10_out, and_5_out);
  LATCHSet_Clear latchset_clear_2 (.C(or_6_out), .S(dec3bit_1_out_6), .Q(out_4[3]));  // open: nQ
  LATCHSet_Clear latchset_clear_3 (.C(or_7_out), .S(dec3bit_1_out_5), .Q(out_4[2]));  // open: nQ
  LATCHSet_Clear latchset_clear_4 (.C(or_8_out), .S(dec3bit_1_out_4), .Q(out_4[1]));  // open: nQ
  LATCHSet_Clear latchset_clear_5 (.C(or_9_out), .S(or_4_out), .Q(out_4[0]));  // open: nQ
  and and_1 (and_1_out, up, out_4[4], out_4[3]);
  and and_2 (and_2_out, up, out_4[3], out_4[2]);
  and and_3 (and_3_out, up, out_4[2], out_4[1]);
  and and_4 (and_4_out, up, out_4[1], out_4[0]);
  and and_5 (and_5_out, up, out_4[0], out_4[4]);
  and and_6 (and_6_out, down, out_4[4], out_4[0]);
  and and_7 (and_7_out, down, out_4[3], out_4[4]);
  and and_8 (and_8_out, down, out_4[2], out_4[3]);
  and and_9 (and_9_out, down, out_4[1], out_4[2]);
  and and_10 (and_10_out, down, out_4[0], out_4[1]);

  // Other names for the same wires on the sheet: _4 = out_4[0]; _3 = out_4[1]; _2 = out_4[2]; _1 = out_4[3];
  //   _0 = out_4[4]
endmodule

module Lose (
  input  [4:0] in_1,
  input  [4:0] in_2,
  input  in_3,
  output out_4
);

  wire comparator_1_eq;

  Comparator #(.width(5)) comparator_1 (.a(in_1), .b(in_2), .eq(comparator_1_eq));  // open: gt, lt
  LATCHSet_Clear latchset_clear_1 (.C(in_3), .S(comparator_1_eq), .Q(out_4));  // open: nQ
endmodule
